# Fritzing sketch ek2 (saved by Fritzing 0.9.1b)
breadboards: 1

parts:
  Part1 = Pro Trinket 5V
  Q1 = NPN-Transistor [package="TO92 [THT]"]
  R1 = Resistor [tolerance=±5% resistance=220 package=THT]
  SPKR1 = Loudspeaker
  S1 = Pushbutton [package="[THT]"]
  S2 = Pushbutton [package="[THT]"]

nets:
  N1: Part1.GND, SPKR1.pin1, S1.Pin_3, S1.Pin_4, S2.Pin_3, S2.Pin_4
  N2: Part1.VBUS, Q1.C
  N3: Part1.D6, S2.Pin_1, S2.Pin_2
  N4: Part1.D4, S1.Pin_1, S1.Pin_2
  N5: Part1.D11, R1.Pin_1
  N6: Q1.E, SPKR1.pin2
  N7: Q1.B, R1.Pin_0

custom parts:
  Pro Trinket 5V: The Pro Trinket 5V is like an Arduino Pro Mini with more pins and USB included. Built with the common core Arduino chip, the ATmega328p, it has 18 GPIO, 2 extra analog inputs, 28K of flash, and 2K of RAM. It has onboard USB bootloading support with Optiboot support, so you can either program your Pro Trinket over USB or with a FTDI cable. The Pro Trinket is programmable using the Arduino IDE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
